# Fritzing sketch atelier EX 3 (saved by Fritzing 0.9.3b)
breadboards: 1

parts:
  Part1 = Arduino Uno (Rev3)
  R1 = Resistor [tolerance=±5% resistance=1M package="2010 [SMD]"]
  R2 = Resistor [tolerance=±5% resistance=1k package="0402 [SMD]"]
  R3 = Resistor [tolerance=±5% resistance=220 package=THT]
  R4 = Textile Stretch Sensor [part_number=PW052]
  R5 = Textile Analog Pressure Sensor [part_number=PW073]
  R6 = Textile Analog Pressure Sensor [part_number=PW073]  # not connected

nets:
  N1: Part1.A0, R2.Pin_0, R4.pin_1
  N2: Part1.A2, R3.Pin_0, R5.pin_0
  N3: Part1.GND, R2.Pin_1, R3.Pin_1
  N4: Part1.D2, R1.Pin_1
  N5: Part1.D4, R1.Pin_0
  N6: Part1.5V, R4.pin_0, R5.pin_1
